# Fritzing sketch MoodyWoody (saved by Fritzing 0.9.3b)
breadboards: 2

parts:
  S1 = Pushbutton [package="[THT]"]
  S2 = Pushbutton [package="[THT]"]
  R1 = Resistor [tolerance=±5% resistance=220 package="1206 [SMD]"]
  R2 = Resistor [tolerance=±5% resistance=220 package="1206 [SMD]"]
  R3 = Resistor [tolerance=±5% resistance=220 package="1206 [SMD]"]
  R4 = Resistor [tolerance=±5% resistance=220 package="1206 [SMD]"]
  R5 = Resistor [tolerance=±5% resistance=220 package="1206 [SMD]"]
  R6 = Resistor [tolerance=±5% resistance=220 package="1206 [SMD]"]
  R7 = Resistor [tolerance=±5% resistance=220 package="1206 [SMD]"]
  R8 = Resistor [tolerance=±5% resistance=220 package="1206 [SMD]"]
  R9 = Resistor [tolerance=±5% resistance=220 package="1206 [SMD]"]
  R10 = Resistor [tolerance=±5% resistance=220 package="1206 [SMD]"]
  LED27 = smd LED [color="Red (633nm)" package="1206 [SMD]"]
  LED44 = smd LED [color="Red (633nm)" package="1206 [SMD]"]
  LED45 = smd LED [color="Red (633nm)" package="1206 [SMD]"]
  LED46 = smd LED [color="Red (633nm)" package="1206 [SMD]"]
  LED47 = smd LED [color="Red (633nm)" package="1206 [SMD]"]
  LED48 = smd LED [color="Red (633nm)" package="1206 [SMD]"]
  Part1 = Arduino Mega ADK (Rev3)
  R11 = Resistor [tolerance=±5% resistance=220 package="1206 [SMD]"]
  R12 = Resistor [tolerance=±5% resistance=220 package="1206 [SMD]"]
  LED50 = smd LED [color="Red (633nm)" package="1206 [SMD]"]
  LED51 = smd LED [color="Red (633nm)" package="1206 [SMD]"]
  LED52 = smd LED [color="Red (633nm)" package="1206 [SMD]"]
  LED53 = smd LED [color="Red (633nm)" package="1206 [SMD]"]
  LED54 = smd LED [color="Red (633nm)" package="1206 [SMD]"]
  LED55 = smd LED [color="Red (633nm)" package="1206 [SMD]"]
  LED56 = smd LED [color="Red (633nm)" package="1206 [SMD]"]
  LED57 = smd LED [color="Red (633nm)" package="1206 [SMD]"]
  LED58 = smd LED [color="Red (633nm)" package="1206 [SMD]"]
  LED59 = smd LED [color="Red (633nm)" package="1206 [SMD]"]
  LED60 = smd LED [color="Red (633nm)" package="1206 [SMD]"]
  LED61 = smd LED [color="Red (633nm)" package="1206 [SMD]"]
  LED62 = smd LED [color="Red (633nm)" package="1206 [SMD]"]
  LED63 = smd LED [color="Red (633nm)" package="1206 [SMD]"]

nets:
  N1: S1.Pin_1, S1.Pin_2, Part1.D13_PWM, R11.Pin_0
  N2: S1.Pin_3, S1.Pin_4, S2.Pin_1, S2.Pin_2, Part1.5V
  N3: S2.Pin_3, S2.Pin_4, Part1.D19/RX1, R12.Pin_1
  N4: R1.Pin_0, LED44.cathode, LED59.cathode
  N5: R1.Pin_1, R2.Pin_1, R3.Pin_1, R4.Pin_1, R5.Pin_1, R6.Pin_0, R7.Pin_0, R8.Pin_0, R9.Pin_0, R10.Pin_0, Part1.GND, R11.Pin_1, R12.Pin_0
  N6: R2.Pin_0, LED45.cathode, LED60.cathode
  N7: R3.Pin_0, LED46.cathode, LED61.cathode
  N8: R4.Pin_0, LED47.cathode, LED62.cathode
  N9: R5.Pin_0, LED48.cathode, LED63.cathode
  N10: R6.Pin_1, LED50.cathode, LED54.cathode
  N11: R7.Pin_1, LED27.cathode, LED55.cathode
  N12: R8.Pin_1, LED51.cathode, LED56.cathode
  N13: R9.Pin_1, LED52.cathode, LED57.cathode
  N14: R10.Pin_1, LED53.cathode, LED58.cathode
  N15: LED27.anode, Part1.D38
  N16: LED44.anode, Part1.D11_PWM
  N17: LED45.anode, Part1.D9_PWM
  N18: LED46.anode, Part1.D6_PWM
  N19: LED47.anode, Part1.D3_PWM
  N20: LED48.anode, Part1.D15/RX3
  N21: Part1.D14/TX3, LED63.anode
  N22: Part1.D12_PWM, LED59.anode
  N23: Part1.D10_PWM, LED60.anode
  N24: Part1.D4_PWM, LED62.anode
  N25: Part1.D7_PWM, LED61.anode
  N26: Part1.D22, LED58.anode
  N27: Part1.D25, LED53.anode
  N28: Part1.D28, LED51.anode
  N29: Part1.D30, LED56.anode
  N30: Part1.D33, LED57.anode
  N31: Part1.D34, LED52.anode
  N32: Part1.D40, LED55.anode
  N33: Part1.D44, LED50.anode
  N34: Part1.D46, LED54.anode
